# Fritzing sketch wiring-diagram (saved by Fritzing 0.9.6b)
breadboards: 1

parts:
  HITACHI_HD44780U = LCD screen
  U3 = POT [package=trim_pot]
  Raspberry_PI_Zero_W = Raspberry Pi Zero

nets:
  N1: HITACHI_HD44780U.VSS, HITACHI_HD44780U.R/W, HITACHI_HD44780U.LED-, U3.S, Raspberry_PI_Zero_W.pin_6, Raspberry_PI_Zero_W.pin_9, Raspberry_PI_Zero_W.pin_39
  N2: HITACHI_HD44780U.VDD, Raspberry_PI_Zero_W.pin_2, Raspberry_PI_Zero_W.pin_4
  N3: HITACHI_HD44780U.V0, U3.E
  N4: HITACHI_HD44780U.RS, Raspberry_PI_Zero_W.pin_37
  N5: HITACHI_HD44780U.E, Raspberry_PI_Zero_W.pin_35
  N6: HITACHI_HD44780U.DB4, Raspberry_PI_Zero_W.pin_33
  N7: HITACHI_HD44780U.DB5, Raspberry_PI_Zero_W.pin_31
  N8: HITACHI_HD44780U.DB6, Raspberry_PI_Zero_W.pin_29
  N9: HITACHI_HD44780U.DB7, Raspberry_PI_Zero_W.pin_27
  N10: HITACHI_HD44780U.LED+, Raspberry_PI_Zero_W.pin_23

// code stored in the sketch: 1.ino

